# Fritzing sketch Diagrama (saved by Fritzing 0.9.3b)
breadboards: 1

parts:
  S1 = Pushbutton [package="[THT]"]
  LED1 = LED - 5mm [color="Red (633nm)" package="5 mm [THT]"]  # not connected
  Componente1 = Arduino Uno (Rev3)
  Raspberry_Pi_1 = Raspberry Pi 3 [part_number=RPI-3-V1.2]  # not connected
  R1 = Resistor [tolerance=±5% resistance=1 power=1W package=THT]
  Componente2 = Breakout Board for Electret Microphone  # not connected
  CNY1 = CNY70  # not connected
  R2 = Resistor [tolerance=±5% resistance=220 package=THT]  # not connected
  M1 = Dagu DGServo 9g (Top view) [part_number=RS001B]

nets:
  N1: S1.Pin_1, S1.Pin_2
  N2: S1.Pin_3, S1.Pin_4
  N3: Componente1.A0, R1.Pin_1, M1.vcc
  N4: Componente1.D8, M1.pulse
  GND: Componente1.GND, M1.gnd

custom parts:
  CNY70: Sensor de Infrarojos de corto alcance.
