# Fritzing sketch Diagrama_v2 (saved by Fritzing 0.9.3b)
circuit board: 8.46667cm x 5.64444cm
breadboards: 1

parts:
  S1 = Pushbutton [package="[THT]"]
  Arduino = Arduino Uno (Rev3)
  Raspberry_Pi_1 = Raspberry Pi 3 [part_number=RPI-3-V1.2]
  R1 = Resistor [tolerance=±5% resistance=1 power=1W package=THT]
  Sensor_Sonido = Breakout Board for Electret Microphone
  Servo = Dagu DGServo 9g (Top view) [part_number=SG90]
  LED4 = LED - 5mm [color="Red (633nm)" package="5 mm [THT]"]
  LED1 = LED - 5mm [color="Yellow (595nm)" package="5 mm [THT]"]
  LED2 = LED - 5mm [color="Green (570nm)" package="5 mm [THT]"]
  LED3 = LED - 5mm [color="White (4500K)" package="5 mm [THT]"]
  R6 = Resistor [tolerance=±5% resistance=1k package="0402 [SMD]"]
  R4 = Resistor [tolerance=±5% resistance=1k package="0402 [SMD]"]
  R3 = Resistor [tolerance=±5% resistance=1k package="0402 [SMD]"]
  R5 = Resistor [tolerance=±5% resistance=1k package="0402 [SMD]"]
  R2 = Resistor [tolerance=±5% resistance=1k package="0402 [SMD]"]
  SP1 = SPEAKER [package=pcb_mount_speaker]  # not connected
  J1 = Infrared Proximity Sensor [part_number="Sensor Infrarrojo"]

nets:
  VCC: S1.Pin_1, S1.Pin_2, Raspberry_Pi_1.5V, Sensor_Sonido.VCC, J1.Vcc
  N1: S1.Pin_3, S1.Pin_4, Raspberry_Pi_1.GPIO24, R2.Pin_0
  N2: Arduino.A0, R1.Pin_1, Servo.vcc
  N3: Arduino.D9_PWM, Servo.pulse
  N4: Arduino.5V, R1.Pin_0
  GND: Arduino.GND, Servo.gnd
  GND_2: Raspberry_Pi_1.GND, Sensor_Sonido.GND, R6.Pin_1, R4.Pin_1, R3.Pin_1, R5.Pin_1, R2.Pin_1, J1.GND
  N5: Raspberry_Pi_1.GPIO6, LED3.anode
  N6: Raspberry_Pi_1.GPIO26, J1.Vout
  N7: Raspberry_Pi_1.GPIO21, LED1.anode
  N8: Raspberry_Pi_1.GPIO20, LED2.anode
  N9: Raspberry_Pi_1.GPIO16, LED4.anode
  N10: Raspberry_Pi_1.GPIO25, Sensor_Sonido.AUD
  N11: LED4.cathode, R6.Pin_0
  N12: LED1.cathode, R3.Pin_0
  N13: LED2.cathode, R4.Pin_0
  N14: LED3.cathode, R5.Pin_0

notes:
  GPIO_LED_ROJO = 16
  GPIO_LED_VERDE = 20
  GPIO_MICROFONO = 25
  GPIO_LED_AMARILLO = 21
  GPIO_LED_BLANCO = 6
  GPIO_LED_PRESENCIA = GPIO_LED_BLANCO
  GPIO_INFRARROJO = 26
  GPIO_PULSADOR = 24
